# Fritzing sketch board (saved by Fritzing 0.9.3b)
breadboards: 3

parts:
  Part3 = RFID-RC522-v2
  R1 = Resistor [tolerance=±5% resistance=220 package=THT]
  R2 = Trimmer Potentiometer [maximum_resistance=10kΩ package=THT]
  LED1 = LED - 5mm [color="Blue (470nm)" package="5 mm [THT]"]
  U1 = 74HC595 [package="DIP16 [THT]"]
  LCD1 = LCD screen
  R3 = Resistor [tolerance=±5% resistance=220 package=THT]
  R4 = Resistor [tolerance=±5% resistance=220 package=THT]
  R5 = Resistor [tolerance=±5% resistance=220 package=THT]
  R6 = Resistor [tolerance=±5% resistance=220 package=THT]
  R8 = Resistor [tolerance=±5% resistance=220 package=THT]
  LED2 = LED - 5mm [color="Blue (470nm)" package="5 mm [THT]"]
  LED3 = LED - 5mm [color="Green (555nm)" package="5 mm [THT]"]
  LED4 = LED - 5mm [color="Green (555nm)" package="5 mm [THT]"]
  LED5 = LED - 5mm [color="Red (633nm)" package="5 mm [THT]"]
  LED6 = LED - 5mm [color="Red (633nm)" package="5 mm [THT]"]
  LED7 = LED - 5mm [color="Yellow (585nm)" package="5 mm [THT]"]
  LED8 = LED - 5mm [color="Yellow (585nm)" package="5 mm [THT]"]
  J1 = Basic Servo
  Part1 = Arduino Uno (Rev3)
  R9 = Resistor [tolerance=±5% resistance=220 package=THT]
  R7 = Resistor [tolerance=±5% resistance=220 package=THT]

nets:
  VCC: Part3.SDA, R2.leg1, U1.MR, U1.VCC, LCD1.VDD, LCD1.LED+, J1.vcc, Part1.5V
  N1: Part3.SCK, Part1.D9_PWM
  GND: Part3.MOSI, R2.leg2, LED1.cathode, U1.OE, LCD1.VSS, LCD1.R/W, LCD1.LED-, LED2.cathode, LED3.cathode, LED4.cathode, LED5.cathode, LED6.cathode, LED7.cathode, LED8.cathode, J1.gnd, Part1.GND
  N2: Part3.IRQ, Part1.D12/MISO
  N3: Part3.GND, Part1.D11_PWM/MOSI
  N4: Part3.RST, Part1.D13/SCK
  N5: Part3.3.3V, Part1.D10_PWM/SS
  N6: R1.Pin_0, U1.Q0
  N7: R1.Pin_1, LED3.anode
  N8: R2.wiper, LCD1.V0
  N9: LED1.anode, R5.Pin_1
  N10: U1.Q1, R4.Pin_0
  N11: U1.Q2, R5.Pin_0
  N12: U1.Q4, R6.Pin_0
  N13: U1.Q5, R7.Pin_0
  N14: U1.Q6, R8.Pin_0
  N15: U1.Q7, R9.Pin_0
  N16: U1.GND, R3.Pin_0
  N17: U1.SH_CP, Part1.A0
  N18: U1.ST_CP, Part1.A1
  N19: U1.DS, Part1.A2
  N20: LCD1.RS, Part1.D3_PWM
  N21: LCD1.E, Part1.D4
  N22: LCD1.DB4, Part1.D5_PWM
  N23: LCD1.DB5, Part1.D6_PWM
  N24: LCD1.DB6, Part1.D7
  N25: LCD1.DB7, Part1.D8
  N26: R3.Pin_1, LED8.anode
  N27: R4.Pin_1, LED4.anode
  N28: R6.Pin_1, LED2.anode
  N29: R8.Pin_1, LED6.anode
  N30: LED5.anode, R7.Pin_1
  N31: LED7.anode, R9.Pin_1
  N32: J1.pulse, Part1.D2

custom parts:
  RFID-RC522-v2: A simple China made RFID-RC522 Reader; do check the pin labels, as this is a MFRC522 based clone.
